# Fritzing sketch SoilMoistureSensor (saved by Fritzing 0.9.4)
breadboards: 1

parts:
  SparkFun_Pro_Micro = SparkFun Pro Micro [part_number=DEV-12640]
  3_7V_Battery = Lithium Ion Polymer Battery 3.7v 2000mAh [part_number=2011]
  SW4 = Pushbutton [package="[SMD]"]
  SW3 = Pushbutton [package="[SMD]"]
  SW2 = Pushbutton [package="[SMD]"]
  SW1 = Pushbutton [package="[SMD]"]
  C1 = Electrolytic Capacitor [capacitance=10µF package="100 mil [THT, electrolytic]"]
  Power_Switch = Toggle Switch [package=THT]
  T1 = LM35 Temperature Sensor [package="TO92 [THT]"]
  OLED = OLED Monochrome 128x64 I2C [part_number=661]
  LDO = TC1262 [chip_label=IC package=SOT-223]
  R1 = Resistor [tolerance=±5% resistance=10k package=THT]
  R3 = Resistor [tolerance=±5% resistance=10k package=THT]
  R4 = Resistor [tolerance=±5% resistance=10k package=THT]
  R2 = Resistor [tolerance=±5% resistance=10k package=THT]
  STATIC = Resistor [tolerance=±5% resistance=10k package=THT]
  HIGH = Resistor [tolerance=±5% resistance=47k package=THT]
  Probe = Screw terminal - 2 pins [package=THT]
  MED = Resistor [tolerance=±5% resistance=68k package=THT]
  LOW = Resistor [tolerance=±5% resistance=100k package=THT]
  LED1 = LED - 5mm [color="Red (633nm)" package="5 mm [THT]"]
  LED2 = LED - 5mm [color="Green (570nm)" package="5 mm [THT]"]
  R9 = Resistor [tolerance=±5% resistance=220 package=THT]
  C2 = Electrolytic Capacitor [capacitance=10µF package="100 mil [THT, electrolytic]"]
  C3 = Electrolytic Capacitor [capacitance=10µF package="100 mil [THT, electrolytic]"]
  C4 = Electrolytic Capacitor [capacitance=10µF package="100 mil [THT, electrolytic]"]
  C5 = Electrolytic Capacitor [capacitance=10µF package="100 mil [THT, electrolytic]"]

nets:
  GND: SparkFun_Pro_Micro.GND, 3_7V_Battery.negative, SW4.Pin_1, SW3.Pin_1, SW3.Pin_2, SW2.Pin_1, SW2.Pin_2, SW1.Pin_1, C1.-, T1.GND, OLED.GND, LDO.pin2, R9.Pin_0, C2.-, C3.-, C4.-, C5.-
  VCC: SparkFun_Pro_Micro.VCC, T1.+Vs, OLED.VCC, LDO.pin3, R1.Pin_0, R3.Pin_0, R4.Pin_0, R2.Pin_0
  N1: SparkFun_Pro_Micro.A1, HIGH.Pin_0, Probe.pin1, MED.Pin_0, LOW.Pin_0
  N2: SparkFun_Pro_Micro.A0, T1.Vout
  N3: SparkFun_Pro_Micro.MISO, LED2.anode
  N4: SparkFun_Pro_Micro.MOSI, LED1.anode
  N5: SparkFun_Pro_Micro.D10, HIGH.Pin_1
  N6: SparkFun_Pro_Micro.D9, MED.Pin_1
  N7: SparkFun_Pro_Micro.D8, LOW.Pin_1
  N8: SparkFun_Pro_Micro.D7, SW3.Pin_3, SW3.Pin_4, R3.Pin_1, C2.+, C5.+
  N9: SparkFun_Pro_Micro.D6, STATIC.Pin_0
  N10: SparkFun_Pro_Micro.D4, SW4.Pin_3, SW4.Pin_4, R4.Pin_1
  N11: SparkFun_Pro_Micro.D3, OLED.SCL
  N12: SparkFun_Pro_Micro.D2, OLED.SDA
  N13: SparkFun_Pro_Micro.RXI, SW2.Pin_3, SW2.Pin_4, R2.Pin_1, C4.+
  N14: SparkFun_Pro_Micro.TXO, SW1.Pin_3, SW1.Pin_4, R1.Pin_1, C3.+
  N15: 3_7V_Battery.positive, Power_Switch.COM
  N16: C1.+, Power_Switch.L1, LDO.pin1
  N17: STATIC.Pin_1, Probe.pin2
  N18: LED1.cathode, LED2.cathode, R9.Pin_1

custom parts:
  SparkFun Pro Micro: This tiny little board does all of the neat-o Arduino tricks that you’re familiar with: 4 channels of 10-bit ADC, 5 PWM pins, 12 DIOs as well as hardware serial connections Rx and Tx. Running at 16MHz and 5V, this board will remind you a lot of your other favorite Arduino-compatible boards but this little guy can go just about anywhere. There is a voltage regulator on board so it can accept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
  Lithium Ion Polymer Battery 3.7v 2000mAh: Lithium ion polymer (also known as 'lipo' or 'lipoly') batteries are thin, light and powerful. The output ranges from 4.2V when completely charged to 3.7V. This battery has a capacity of 2000mAh. The batteries come pre-attached with a genuine 2-pin JST-PH connector as shown and include the necessary protection circuitry.
  OLED Monochrome 128x64 I2C: These displays are small, only about 1" diagonal, but very readable due to the high contrast of an OLED display. This display is made of 128x64 individual white OLED pixels, each one is turned on or off by the controller chip. Because the display makes its own light, no backlight is required. This reduces the power required to run the OLED and is why the display has such high contrast; we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
  TC1262: A 3.3 V low-dropout voltage regulator, part no. TC1262-3.3
